# Fritzing sketch Cartridge (saved by Fritzing 0.9.2b)
circuit board: 1.57578cm x 1.24896cm
breadboards: 1

parts:
  Attiny85 = attiny85 [package=dip]
  SSD1310 = male pin header, 4 pins [form="♂ (male)"]
  SSD1311 = male pin header, 4 pins [form="♂ (male)"]

nets:
  N1: Attiny85.Pin_1, SSD1310.pin4
  N2: Attiny85.Pin_2, SSD1310.pin3
  N3: Attiny85.Pin_3, SSD1310.pin2
  N4: Attiny85.Pin_4, SSD1310.pin1
  N5: Attiny85.Pin_5, SSD1311.pin1
  N6: Attiny85.Pin_6, SSD1311.pin2
  N7: Attiny85.Pin_7, SSD1311.pin3
  N8: Attiny85.Pin_8, SSD1311.pin4

notes:
  .
