# Fritzing sketch TinyGame (saved by Fritzing 0.9.2b)
circuit board: 3cm x 4.2cm
breadboards: 1

parts:
  R = Pushbutton [package="[THT]"]
  L = Pushbutton [package="[THT]"]
  100nF = Ceramic Capacitor [capacitance=100nF package="100 mil [THT, multilayer]"]
  10k = Resistor [tolerance=±5% resistance=10k package=THT]
  10k_2 = Resistor [tolerance=±5% resistance=10k package=THT]
  CR2032 = CR2032
  SSD1306 = female pin header, 4 pins [form="♀ (female)"]
  10k_3 = Resistor [tolerance=±5% resistance=10k package=THT]
  SSD1307 = female pin header, 4 pins [form="♀ (female)"]
  SSD1308 = female pin header, 4 pins [form="♀ (female)"]
  Attiny85 = attiny85 [package=dip]
  RST = Pushbutton [package="[THT]"]
  ON = Toggle Switch [package=THT]
  BUZ = Piezo Speaker

nets:
  VCC: R.Pin_1, R.Pin_2, L.Pin_3, L.Pin_4, 100nF.0, 10k.Pin_0, 10k_2.Pin_0, SSD1306.pin1, 10k_3.Pin_0, SSD1308.pin4, Attiny85.Pin_8, ON.COM
  N1: R.Pin_3, R.Pin_4, SSD1308.pin3, Attiny85.Pin_7
  N2: L.Pin_1, L.Pin_2, SSD1308.pin1, Attiny85.Pin_5
  GND: 100nF.1, 10k.Pin_1, 10k_2.Pin_1, CR2032.-, SSD1306.pin2, SSD1307.pin1, Attiny85.Pin_4, RST.Pin_1, RST.Pin_2, ON.L2, BUZ.pin1
  N3: CR2032.+, ON.L1
  N4: SSD1306.pin3, SSD1307.pin3, Attiny85.Pin_2
  N5: SSD1306.pin4, SSD1307.pin2, Attiny85.Pin_3
  N6: 10k_3.Pin_1, SSD1307.pin4, Attiny85.Pin_1, RST.Pin_3, RST.Pin_4
  N7: SSD1308.pin2, Attiny85.Pin_6, BUZ.pin2

notes:
  .
  Based on the work of
  http://webboggles.com/attiny85-breakout-keychain-game/
  This version has been improved with the addition of reset button, this way it is possible to reset the system in case of an infinite loop or similar bug in the software. Additionally, a switch to completely power-off the device has been added. And a 100nF capacitor to improve VCC/GND connection of Attiny85 chip.
  gnd
  3V
  GND
  CLK
  DAT

custom parts:
  CR2032: CR2032 coin cell PCB adapter
