# Fritzing sketch TinyGame2B (saved by Fritzing 0.9.2b)
circuit board: 3cm x 4.2cm
breadboards: 1

parts:
  R = Pushbutton [package="[THT]"]
  10k = Resistor [tolerance=±5% resistance=10k package=THT]
  SSD1306 = female pin header, 4 pins [form="♀ (female)"]
  10k_2 = Resistor [tolerance=±5% resistance=10k package=THT]
  RST = Pushbutton [package="[THT]"]
  PWR = Toggle Switch [package=THT]
  BUZ = Piezo Speaker
  Attiny85 = attiny85 [package=dip]
  100nF = Ceramic Capacitor [capacitance=100nF package="100 mil [THT, multilayer]"]
  10k_3 = Resistor [tolerance=±5% resistance=10k package=THT]
  CR2032 = CR2032
  L = Pushbutton [package="[THT]"]

nets:
  N1: R.Pin_1, R.Pin_2, 10k.Pin_0, Attiny85.Pin_7
  VCC: R.Pin_3, R.Pin_4, SSD1306.pin1, 10k_2.Pin_0, PWR.COM, Attiny85.Pin_8, 100nF.0, L.Pin_3, L.Pin_4
  GND: 10k.Pin_1, SSD1306.pin2, RST.Pin_1, RST.Pin_2, PWR.L2, BUZ.pin1, Attiny85.Pin_4, 100nF.1, 10k_3.Pin_1, CR2032.-
  N2: SSD1306.pin3, Attiny85.Pin_2
  N3: SSD1306.pin4, Attiny85.Pin_3
  N4: 10k_2.Pin_1, RST.Pin_3, RST.Pin_4, Attiny85.Pin_1
  N5: PWR.L1, CR2032.+
  N6: BUZ.pin2, Attiny85.Pin_6
  N7: Attiny85.Pin_5, 10k_3.Pin_0, L.Pin_1, L.Pin_2

notes:
  .
  Based on the work of
  http://webboggles.com/attiny85-breakout-keychain-game/
  This version has been improved with the addition of reset button, this way it is possible to reset the system in case of an infinite loop or similar bug in the software. Additionally, a switch to completely power-off the device has been added, which allow safe replacement of the chip without disconnecting the battery. A 100nF capacitor to improve VCC/GND connection of Attiny85 chip.
  gnd
  3V
  GND
  CLK
  DAT
  TinyGame
  v0.1 (2016)
  original idea by Ilya Titov
  designed by PAKOZM

custom parts:
  CR2032: CR2032 coin cell PCB adapter
