# Fritzing sketch TinyGame4B (saved by Fritzing 0.9.2b)
circuit board: 3cm x 4.2cm
breadboards: 1

parts:
  100nF = Ceramic Capacitor [capacitance=100nF package="100 mil [THT, multilayer]"]
  CR2032 = CR2032
  SSD1306 = female pin header, 4 pins [form="♀ (female)"]
  10k = Resistor [tolerance=±5% resistance=10k package=THT]
  RST = Pushbutton [package="[THT]"]
  ON = Toggle Switch [package=THT]
  BUZ = Piezo Speaker
  Attiny85 = attiny85 [package=dip]
  U = Pushbutton [package=THT]
  L = Pushbutton [package=THT]
  R = Pushbutton [package=THT]
  D = Pushbutton [package=THT]
  3_3k = Resistor [tolerance=±5% resistance=3.3k package=THT]
  3_3k_2 = Resistor [tolerance=±5% resistance=3.3k package=THT]
  3_3k_3 = Resistor [tolerance=±5% resistance=3.3k package=THT]
  3_3k_4 = Resistor [tolerance=±5% resistance=3.3k package=THT]

nets:
  VCC: 100nF.0, SSD1306.pin1, 10k.Pin_0, ON.COM, Attiny85.Pin_8, 3_3k.Pin_1, 3_3k_4.Pin_1
  GND: 100nF.1, CR2032.-, SSD1306.pin2, RST.Pin_1, RST.Pin_2, ON.L2, BUZ.pin1, Attiny85.Pin_4, U.leg1, L.leg0, R.leg0, D.leg1
  N1: CR2032.+, ON.L1
  N2: SSD1306.pin3, Attiny85.Pin_2
  N3: SSD1306.pin4, Attiny85.Pin_3
  N4: 10k.Pin_1, RST.Pin_3, RST.Pin_4, Attiny85.Pin_1
  N5: BUZ.pin2, Attiny85.Pin_6
  N6: Attiny85.Pin_5, U.leg0, 3_3k_3.Pin_0, 3_3k_4.Pin_0
  N7: Attiny85.Pin_7, R.leg1, 3_3k.Pin_0, 3_3k_2.Pin_0
  N8: L.leg1, 3_3k_2.Pin_1
  N9: D.leg0, 3_3k_3.Pin_1

notes:
  .
  Based on the work of
  http://webboggles.com/attiny85-breakout-keychain-game/
  This version has been improved with the addition of reset button, this way it is possible to reset the system in case of an infinite loop or similar bug in the software. Additionally, a switch to completely power-off the device has been added. And a 100nF capacitor to improve VCC/GND connection of Attiny85 chip. Four buttons are available using the voltage divider trick and analogic inputs.
  gnd
  3V
  GND
  CLK
  DAT

custom parts:
  CR2032: CR2032 coin cell PCB adapter
