# Fritzing sketch TinyGameJoystick (saved by Fritzing 0.9.0b)
circuit board: 4.1cm x 5.6cm
breadboards: 1

parts:
  SSD1306 = female pin header, 4 pins [form="♀ (female)"]
  BUZ = Piezo Speaker
  100nF = Ceramic Capacitor [capacitance=100nF package="100 mil [THT, multilayer]"]
  COM-09032 = Thumb Joystick [package=joystick]
  CR2032 = CR2032
  ATTiny84 = IC, DIP package, 14 pins [chip_label=ATTiny84]
  BTN-B = Pushbutton [package="[THT]"]
  BTN-A = Pushbutton [package="[THT]"]

nets:
  VCC: SSD1306.pin1, 100nF.1, COM-09032.V+, COM-09032.H+, CR2032.+, ATTiny84.pin1, ATTiny84.pin4
  GND: SSD1306.pin2, BUZ.pin1, 100nF.0, COM-09032.SEL-, COM-09032.H-, COM-09032.V-, CR2032.-, ATTiny84.pin14, BTN-B.Pin_1, BTN-B.Pin_2, BTN-A.Pin_1, BTN-A.Pin_2
  N1: SSD1306.pin3, ATTiny84.pin11
  N2: SSD1306.pin4, ATTiny84.pin10
  N3: BUZ.pin2, ATTiny84.pin12
  N4: COM-09032.SEL+, ATTiny84.pin5
  N5: COM-09032.V, ATTiny84.pin6
  N6: COM-09032.H, ATTiny84.pin7
  N7: ATTiny84.pin8, BTN-A.Pin_3, BTN-A.Pin_4
  N8: ATTiny84.pin9, BTN-B.Pin_3, BTN-B.Pin_4

notes:
  .
  Based on the work of
  http://webboggles.com/attiny85-breakout-keychain-game/
  This version has been improved with the addition of joystick with 2 analog axis and one select button, and two action buttons (A and B). A 100nF capacitor to decouple VCC/GND connection of Attiny85 chip. All buttons needs internal pull-up resistors, so they are connected to GND when pushed and open otherwise.
  gnd
  3V
  GND
  CLK
  DAT
  TinyGameJ
  v0.1 (2016)
  designed by PAKOZM
  original idea by Ilya Titov
  in collaboration with Matej

custom parts:
  CR2032: CR2032 coin cell PCB adapter
